# Fritzing sketch circuit (saved by Fritzing 0.9.3b)
breadboards: 1

parts:
  Part1 = Adafruit Metro with Headers [part_number="Adafruit #2488"]
  Part2 = Adafruit Metro with Headers [part_number="Adafruit #2488"]
  Part3 = Adafruit DRV8833 DC/Stepper Motor Driver [part_number="Adafruit #3297"]
  VCC1 = Battery
  VCC2 = Battery
  VCC3 = Battery
  S1 = Toggle Switch [package=THT]
  Part4 = OLED Monochrome 128x64 0.96 inch [part_number=326]
  M1 = DC Motor
  M2 = DC Motor
  Part5 = Adafruit LSM303DLHC Triple-axis Accelerometer+Magnetometer (Compass) [part_number="Adafruit #1120"]
  hc-sr1 = hc-sr04

nets:
  N1: Part1.AD5/SCL, Part5.SCL
  N2: Part1.AD4/SDA, Part5.SDA
  GND: Part1.GND, Part2.GND, Part3.GND, S1.L2, Part4.GND, Part5.GND, hc-sr1.GND
  N3: Part1.MISO, Part3.AIN1
  N4: Part1.MOSI, Part3.AIN2
  N5: Part1.SS, Part3.!SLEEP
  N6: Part1.IO9, Part3.BIN2
  N7: Part1.IO8, Part3.BIN1
  N8: Part1.IO4, hc-sr1.Trig
  N9: Part1.IO3, hc-sr1.Echo
  N10: Part1.IO2, Part2.SS
  N11: Part1.IO1, Part2.IO0
  N12: Part1.IO0, Part2.IO1
  3.3V: Part1.3.3V, Part5.VIN
  +5V: Part1.+5V, hc-sr1.VCC
  VIN: Part1.VIN, Part2.VIN, VCC1.+
  N13: Part2.AD5/SCL, Part4.SCLK_SCK
  N14: Part2.AD4/SDA, Part4.MOSI_SDA
  N15: Part2.IO4, Part4.RESET
  3.3V_2: Part2.3.3V, Part4.VIN
  N16: Part3.PWRIN, VCC1.-, VCC3.+
  N17: Part3.AOUT2, M2.pin_1
  N18: Part3.AOUT1, M2.pin_2
  N19: Part3.BOUT1, M1.pin_1
  N20: Part3.BOUT2, M1.pin_2
  N21: VCC2.-, S1.COM
  N22: VCC2.+, VCC3.-

custom parts:
  Adafruit Metro with Headers: We sure love the ATmega328 here at Adafruit, and we use them a lot for our own projects. The processor has plenty of GPIO, Analog inputs, hardware UART SPI and I2C, timers and PWM galore - just enough for most simple projects. When we need to go small, we use a Pro Trinket 3V or 5V, but when size isn't as much of a concern, and an USB-serial converter is required, we reach for an Adafruit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
  Adafruit DRV8833 DC/Stepper Motor Driver: Spin two DC motors or step one bi-polar or uni-polar stepper with up to 1.2A per channel using the DRV8833. This motor driver chip is a nice alternative to the TB6612 driver. Like that chip, you get 2 full H-bridges, but this chip is better for low voltage uses (can run from 2.7V up to 10.8V motor power) and has built in current limiting capability. We set it up for 1A current limiting so you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
  OLED Monochrome 128x64 0.96 inch: These displays are small, only about 1" diameter, but very readable due to the high contrast of an OLED display. This display is made of 128x64 individual white OLED pixels, each one is turned on or off by the controller chip. Because the display makes its own light, no backlight is required. This reduces the power required to run the OLED and is why the display has such high contrast; we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
  Adafruit LSM303DLHC Triple-axis Accelerometer+Magnetometer (Compass): He told you "Go West, young maker!" - but you don't know which way is West! Ah, if only you had this triple-axis accelerometer/magnetometer compass module. Inside are two sensors, one is a classic 3-axis accelerometer, which can tell you which direction is down towards the Earth (by measuring gravity). The other is a magnetometer that can sense where the strongest magnetic force is coming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
